// Logisim project finalCircuit.circ as structural Verilog
module NextStateLogic (
  input  [4:0] CurrentState,
  input  [3:0] Instruction,
  output [4:0] NextState
);

  wire and_1_out, and_2_out, and_3_out, and_4_out, and_6_out, and_7_out, and_8_out, and_9_out, not_1_out,
       not_2_out, not_3_out, not_4_out;

  not not_1 (not_1_out, CurrentState[4]);
  not not_2 (not_2_out, CurrentState[2]);
  not not_3 (not_3_out, CurrentState[1]);
  not not_4 (not_4_out, CurrentState[0]);
  and and_1 (and_1_out, CurrentState[3], not_2_out, not_3_out, not_4_out);
  and and_2 (and_2_out, not_1_out, CurrentState[1]);
  and and_3 (and_3_out, CurrentState[3], not_2_out, not_3_out, not_4_out);
  and and_4 (and_4_out, not_1_out, CurrentState[1], Instruction[3]);
  and and_5 (NextState[2], not_1_out, CurrentState[1], Instruction[2]);
  and and_6 (and_6_out, not_1_out, CurrentState[1], Instruction[1]);
  and and_7 (and_7_out, not_1_out, CurrentState[0]);
  and and_8 (and_8_out, not_1_out, not_3_out, not_4_out);
  and and_9 (and_9_out, not_1_out, not_4_out, Instruction[0]);
  or or_1 (NextState[4], and_1_out, and_2_out);
  or or_2 (NextState[3], and_3_out, and_4_out);
  or or_3 (NextState[1], and_6_out, and_7_out);
  or or_4 (NextState[0], and_8_out, and_9_out);
endmodule
